# Fritzing sketch iot-arduino-arduinoTimerLibrary (saved by Fritzing 0.9.9b)
circuit board: 7.75924cm x 5.31154cm
breadboards: 1

parts:
  Bauteil1 = Arduino Uno (Rev3)
  S1 = Pushbutton [package="[THT]"]
  LED2_(rot) = LED - 5mm [color="Red (633nm)" current=30mA package="5 mm [THT]"]
  LED1_(grün) = smd LED [color="Green (555nm)" current=0.030 package="0805 [SMD]"]
  R1 = Resistor [tolerance=±5% power=0.25 resistance=220 package=THT]
  R2 = Resistor [tolerance=±5% power=0.25 resistance=220 package=THT]

nets (from the schematic view):
  N1: Bauteil1.D10_PWM/SS, LED1_(grün).anode
  N2: Bauteil1.D12/MISO, LED2_(rot).anode
  N3: Bauteil1.D2, S1.Pin_3, S1.Pin_4
  N4: Bauteil1.GND, S1.Pin_1, S1.Pin_2, R1.Pin_0, R2.Pin_0
  N5: LED2_(rot).cathode, R2.Pin_1
  N6: LED1_(grün).cathode, R1.Pin_1

notes:
  iot-arduino-softwareTimer1
